# Fritzing sketch GPS_xiao (saved by Fritzing 0.9.3b)
circuit board: 8.46667cm x 5.64444cm
breadboards: 1

parts:
  Mod1 = seeeduino-xiao
  Bauteil1 = u-blox NEO-6M GPS Breakout
  OLED1 = OLED 128x64 I2C Monochrome Display
  Bauteil2 = MicroSD Card Module
  S1 = Pushbutton [package="[THT]"]
  R1 = Resistor [tolerance=±5% resistance=10k package=THT]
  Bauteil3 = BME280 Breakout

nets (from the breadboard view):
  N1: Mod1.D2, S1.Pin_1, S1.Pin_2, R1.Pin_1
  N2: Mod1.D3, Bauteil2.CS
  N3: Mod1.D4, OLED1.SCK, Bauteil3.SCK/SCL
  N4: Mod1.D5, OLED1.SDA, Bauteil3.SDI/SDA
  N5: Mod1.D6, Bauteil1.TXD
  N6: Mod1.D7, Bauteil1.RXD
  N7: Mod1.D8, Bauteil2.SCK
  N8: Mod1.D9, Bauteil2.MISO
  N9: Mod1.D10, Bauteil2.MOSI
  VCC: Mod1.3V3, Bauteil1.VCC, OLED1.VDD, Bauteil2.VCC, S1.Pin_3, S1.Pin_4, Bauteil3.3.3V
  GND: Mod1.GND, Bauteil1.GND, OLED1.GND, Bauteil2.GND, R1.Pin_0, Bauteil3.GND

notes:
  3.3 V
  5 V
  Batterie Anschluss

custom parts:
  seeeduino-xiao: Seeeduino XIAO processor board.
